# Fritzing sketch Smart-Room-Controller (saved by Fritzing 0.9.4)
breadboards: 1

parts:
  Teensy_3_1 = Teensy 3.1  # not connected
  WIZ820io1 = WIZ820io [part_number=WIZ820io]
  OLED_I2C1 = OLED 128x64 I2C Monochrome Display
  M1 = BMP280
  Part1 = 12 NeoPixel Ring [part_number=1643]
  Neopixel1 = Adafruit RBG Smart Neopixel [package="DIP (Dual Inline) [THT]"]
  Neopixel2 = Adafruit RBG Smart Neopixel [package="DIP (Dual Inline) [THT]"]
  R1 = Resistor [tolerance=±5% resistance=220 package="0402 [SMD]"]
  RG_encoder1 = SprkFn RG Encoder [package="DIP (Dual Inline) [THT]"]

nets:
  GND: WIZ820io1.GND, WIZ820io1.VIN
  N1: OLED_I2C1.SDA, M1.SDA
  N2: OLED_I2C1.SCK, M1.SCL
  VDD: OLED_I2C1.VDD, M1.VIN
  GND_2: OLED_I2C1.GND, M1.GND, Part1.GND, R1.Pin_0
  N3: Part1.OUT, Neopixel2.In
  N4: Part1.VDD, Neopixel1.+, Neopixel2.+, RG_encoder1.B
  N5: Neopixel1.G, Neopixel2.G
  N6: Neopixel1.In, Neopixel2.O
  N7: R1.Pin_1, RG_encoder1.GND

custom parts:
  BMP280: Temperature Humidity Barometric presure Sensor, I2C
  12 NeoPixel Ring: 12 ultra bright smart LED NeoPixels are arranged in a circle with 1.5" (37mm) outer diameter. The rings are 'chainable' - connect the output pin of one to the input pin of another. Use only one microcontroller pin to control as many as you can chain together! Each LED is addressable as the driver chip is inside the LED. Each one has ~18mA constant current drive so the color will be very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
  SprkFn RG Encoder: SparkFun RG Rotary Encoder
